# Fritzing sketch GPSPotHoleTrack_Squematics (saved by Fritzing 0.9.3b)

parts:
  GPS = Flora GPS
  Tarjeta_Principal = Adafruit Flora [part_number="Adafruit #659"]
  part = LilyPad Button Board
  part_2 = I2C Non-Volatile FRAM 32KB
  part_3 = Sewable CR2032 Battery Holder [package=battery_20mm_pth_compact]
  part_4 = LilyPad Button Board
  part_5 = LilyPad Buzzer
  part_6 = LilyPad Button Board
  U1 = LIPO-110mAh [package=lipo-110]

nets:
  3.3V: GPS.3.3V, Tarjeta_Principal.+3V3, part_2.VCC, U1.+
  GND: GPS.GND, Tarjeta_Principal.GND, part.-, part_2.GND, part_3.-, part_4.-, part_5.-, part_6.-, U1.-
  N1: GPS.RX, Tarjeta_Principal.IO1/TX
  N2: GPS.BAT, part_3.+
  N3: GPS.TX, Tarjeta_Principal.IO0/RX
  N4: Tarjeta_Principal.IO6, part_6.S
  N5: Tarjeta_Principal.IO9, part_4.S
  N6: Tarjeta_Principal.IO10, part_5.+
  N7: Tarjeta_Principal.IO12, part.S
  N8: Tarjeta_Principal.IO2/SDA, part_2.SCL
  N9: Tarjeta_Principal.IO3/SCL, part_2.SDA

custom parts:
  Flora GPS: This module is the best way to add a GPS to your wearable project. It's part of the Adafruit Flora series of wearable electronics, designed specifically for use with the Flora motherboard. Installed on the PCB is the latest of our Ultimate GPS modules, a small, super-thin, low power GPS module with built in data-logging capability!
  Adafruit Flora: FLORA is Adafruit's fully-featured wearable electronics platform. It's a round, sewable, Arduino-compatible microcontroller designed to empower amazing wearables projects. The FLORA is small (1.75" diameter, weighing 4.4 grams). The FLORA has built-in USB support. Built in USB means you plug it in to program it, it just shows up - all you need is a Micro-B USB cable, no additional purchases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
  I2C Non-Volatile FRAM 32KB: With our I2C FRAM breakout board you can add some FRAM storage to your next DIY project. FRAM allows for a lower power usage and a faster write performance. It's excellent for low-power or inconsistent-power datalogging or data buffering where you want to stream data fast while also keeping the data when there's no power. Unlike Flash or EEPROM there's no pages to worry about. Each byte can be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
  Sewable CR2032 Battery Holder: Battery Holders Various common sizes : AA, AAA, 20mm coin cell and 12mm coin cell.
